// Digital circuit Lab02.dig as structural Verilog
module Lab02 (
  input  B,
  input  C,
  input  A,
  input  D,
  output Fa,
  output Fb,
  output Fc,
  output Fd,
  output Fe,
  output Fg,
  output Ff
);

  wire A_t, and_1_out, and_2_out, and_3_out, and_4_out, and_5_out, and_6_out, and_7_out, and_8_out,
       and_9_out, and_10_out, and_11_out, and_12_out, and_13_out, and_14_out, and_15_out, B_t, C_t, D_t,
       Fd_t, Fe_t, Ff_t, Fg_t;

  and and_1 (and_1_out, B_t, D_t);
  and and_2 (and_2_out, A_t, C);
  and and_3 (and_3_out, A_t, B, D);
  and and_4 (and_4_out, A, B_t, C_t);
  and and_5 (and_5_out, B, C);
  Seven_Seg seven_seg_1 (.a(Fa), .b(Fb), .c(Fc), .d(Fd_t), .e(Fe_t), .f(Ff_t), .g(Fg_t), .dp(1'b0));
  or or_1 (Fa, and_1_out, and_2_out, and_3_out, and_4_out, and_5_out);
  not not_1 (A_t, A);
  not not_2 (B_t, B);
  not not_3 (C_t, C);
  not not_4 (D_t, D);
  and and_6 (and_6_out, B_t, D_t);
  and and_7 (and_7_out, B_t, A_t);
  and and_8 (and_8_out, A_t, C_t, D_t);
  and and_9 (and_9_out, A_t, C, D);
  and and_10 (and_10_out, A, C_t, D);
  and and_11 (and_11_out, A, B_t);
  and and_12 (and_12_out, B, A_t);
  and and_13 (and_13_out, D, A_t);
  and and_14 (and_14_out, D, C_t);
  and and_15 (and_15_out, A_t, C_t);
  or or_2 (Fb, and_6_out, and_7_out, and_8_out, and_9_out, and_10_out);
  or or_3 (Fc, and_11_out, and_12_out, and_13_out, and_14_out, and_15_out);
endmodule
